# Fritzing sketch MOBIL 4 BAN (saved by Fritzing 0.8.7b)

parts:
  BAT1 = BC9VPC [package=bc9vpc]
  Part1 = Arduino Nano (Rev3.0)
  M1 = DC Motor
  M2 = DC Motor
  M3 = DC Motor
  M4 = DC Motor
  Part2 = HC-05 [part_number=HC-05 package="breakout board"]
  S1 = H-Bridge with L298N

nets:
  N1: BAT1.V+, S1.GND
  5V: BAT1.V-, Part1.5V, Part2.VCC, S1.12V
  N2: Part1.D1/TX, Part2.RXD
  N3: Part1.D0/RX, Part2.TXD
  N4: Part1.D3, S1.IN1
  N5: Part1.D4, S1.IN2
  N6: Part1.D5, S1.ENA
  N7: Part1.D6, S1.ENB
  N8: Part1.D7, S1.IN3
  N9: Part1.D8, S1.IN4
  GND: Part1.GND, Part2.GND
  N10: M1.pin_1, M2.pin_1, S1.M2-02
  N11: M1.pin_2, M2.pin_2, S1.M2-01
  N12: M3.pin_1, M4.pin_1, S1.M1-02
  N13: M3.pin_2, M4.pin_2, S1.M1-01

notes:
  SUPLAY
  L298N
  KIRI
  KANAN
  ARDUINO NANO
  BLUETOOTH

custom parts:
  HC-05: A commonly available HC-05 Bluetooth breakout board.
  H-Bridge with L298N: h-bridge
