# Fritzing sketch WEMOS OLED SERVO TANGKI (saved by Fritzing 0.8.7b)

parts:
  BAT1 = BC9VPC [package=bc9vpc]
  o1 = Module display OLED I2C 128x64 SSD1306 [package=THT]
  WeMos_D1_Mini1 = WeMos D1 Mini
  J1 = Basic Servo
  J2 = Piezo Speaker

nets:
  GND: BAT1.V+, o1.GND, WeMos_D1_Mini1.G, J1.gnd, J2.pin1
  VCC: BAT1.V-, o1.VCC, WeMos_D1_Mini1.5V, J1.vcc
  N1: o1.SCL, WeMos_D1_Mini1.D1
  N2: o1.SDA, WeMos_D1_Mini1.D2
  N3: WeMos_D1_Mini1.D3, J2.pin2
  N4: WeMos_D1_Mini1.D4, J1.pulse

notes:
  SUPLAY
  OLED
  SERVO
  WEMOS
  BUZZER

custom parts:
  Module display OLED I2C 128x64 SSD1306: Ecran OLED I2C SSD163 de 128x64 avec connexion I2C
